// Digital circuit ROOT.dig as structural Verilog
module ROOT (
);

  wire if_1_p1;

  // IF if_1: pin names not known; wires that end beside it: if_1_p1
  // IFIDReg ifidreg_1: pin names not known; wires that end beside it: if_1_p1
  fb_forwarding_unit #(.applicationType("IVERILOG"), .iverilogOptions("-y /Users/zhangyibo/riscvdesign/RISCVFirebird/Pipeline/rtl \n-I /Users/zhangyibo/riscvdesign/RISCVFirebird/Pipeline/rtl"), .CodeFile("/Users/zhangyibo/riscvdesign/RISCVFirebird/Pipeline/rtl/fb_forwarding_unit.v")) u_fb_forwarding_unit ();  // open: id_ex_register_rs1, id_ex_register_rs2, ex_mem_regwrite, ex_mem_register_rd, mem_wb_regwrite, mem_wb_register_rd, forward_a, forward_b
  IF if_2 ();  // open: PC1, _1, _2, _444
endmodule
